// Logisim project SymulatorProfesora.circ as structural Verilog: 1 circuit, main circuit main
module main (
  input  [15:0] in_1,
  input  in_2,
  input  in_3,
  input  send,
  input  send_2,
  input  send_3,
  input  send_4,
  input  send_5,
  input  send_6
);

  wire and_1_out, clock_1_out, clock_2_out, clock_3_out, comparator_1_eq, comparator_2_eq, main_1_pulse,
       main_9_catch, main_10_catch, main_11_catch, main_12_catch, main_13_catch, main_14_catch, main_15_done,
       or_1_out, or_3_out;
  wire [4:0] adder_1_out, counter_1_q, counter_2_q, register_1_q;
  wire [6:0] keyboard_1_data, main_2_output;
  wire [9:0] counter_3_q, counter_4_q, multiplier_1_out;
  wire [23:0] rom_8_data;
  wire [31:0] main_3_output, main_4_output, main_5_output, main_6_output, main_7_output, main_8_output,
       main_15_out_4, main_15_out_5, main_15_out_6, main_15_out_7, main_15_out_8, main_15_out_9,
       main_15_out_10, main_15_out_11, main_15_out_12, main_15_out_13, main_15_out_14, main_15_out_15,
       main_15_out_16, main_15_out_17, main_15_out_18, main_15_out_19, main_15_out_20, main_15_out_21,
       main_15_out_22, main_15_out_23, main_15_out_24, main_15_out_25, main_15_out_26, main_15_out_27,
       main_15_out_28, main_15_out_29, main_15_out_30, main_15_out_31, main_15_out_32, main_15_out_33,
       main_15_out_34, main_15_out_35, or_2_out, rom_1_data, rom_2_data, rom_3_data, rom_4_data, rom_5_data,
       rom_6_data, rom_7_data;

  Keyboard #(.buflen(1)) keyboard_1 (.clk(clock_1_out), .re(1'b1), .data(keyboard_1_data));  // open: clr, avail
  Comparator #(.width(7), .mode("unsigned")) comparator_1 (
    .a(keyboard_1_data), .b(7'b1100100), .eq(comparator_1_eq));  // open: gt, lt
  Comparator #(.width(7), .mode("unsigned")) comparator_2 (
    .a(keyboard_1_data), .b(7'b1100001), .eq(comparator_2_eq));  // open: gt, lt
  Counter #(.width(5), .max('h1b), .ongoal("stay")) counter_1 (
    .load(comparator_1_eq), .Q(counter_1_q), .clk(or_1_out));  // open: D, count, carry, clr
  or or_1 (or_1_out, comparator_1_eq, comparator_2_eq);
  Counter #(.width(5), .max('h1f)) counter_2 (.Q(counter_2_q), .clk(clock_1_out));  // open: load, D, count, carry, clr
  Clock clock_1 (.out(clock_1_out));
  Register #(.width(5)) register_1 (.D(counter_1_q), .Q(register_1_q), .clk(main_15_done));  // open: en, clr
  Clock clock_2 (.out(clock_2_out));
  Adder #(.width(5)) adder_1 (.a(register_1_q), .b(counter_2_q), .out(adder_1_out));  // open: cin, cout
  comparator_score_thresholds_main main_1 (
    .score(in_1), .reset(in_2), .pulse(main_1_pulse), .clk(clock_2_out));  // open: out
  ROM #(.addrWidth(5), .dataWidth(32)) rom_1 (.addr(adder_1_out), .data(rom_1_data));  // open: sel
  ROM_message_spitter_main main_2 (.clock(clock_2_out), .\output (main_2_output), .trigger(main_1_pulse), .reset(in_3));
  ROM #(.addrWidth(5), .dataWidth(32)) rom_2 (.addr(counter_2_q), .data(rom_2_data));  // open: sel
  ROM #(.addrWidth(5), .dataWidth(32)) rom_3 (.addr(counter_2_q), .data(rom_3_data));  // open: sel
  ROM #(.addrWidth(5), .dataWidth(32)) rom_4 (.addr(counter_2_q), .data(rom_4_data));  // open: sel
  ROM #(.addrWidth(5), .dataWidth(32)) rom_5 (.addr(counter_2_q), .data(rom_5_data));  // open: sel
  ROM #(.addrWidth(5), .dataWidth(32)) rom_6 (.addr(counter_2_q), .data(rom_6_data));  // open: sel
  ROM #(.addrWidth(5), .dataWidth(32)) rom_7 (.addr(counter_2_q), .data(rom_7_data));  // open: sel
  Clock #(.highDuration(64), .lowDuration(64)) clock_3 (.out(clock_3_out));
  TTY #(.rows(1), .cols(110)) tty_1 (.data(main_2_output), .clk(clock_2_out), .clr(main_1_pulse));  // open: we
  student_drop_main main_3 (
    .\input (rom_2_data), .send(send), .\output (main_3_output), .catch(main_9_catch), .clk(clock_3_out));
  student_drop_main main_4 (
    .\input (rom_3_data), .send(send_2), .\output (main_4_output), .catch(main_10_catch), .clk(clock_3_out));
  student_drop_main main_5 (
    .\input (rom_4_data), .send(send_3), .\output (main_5_output), .catch(main_11_catch), .clk(clock_3_out));
  student_drop_main main_6 (
    .\input (rom_5_data), .send(send_4), .\output (main_6_output), .catch(main_12_catch), .clk(clock_3_out));
  student_drop_main main_7 (
    .\input (rom_6_data), .send(send_5), .\output (main_7_output), .catch(main_13_catch), .clk(clock_3_out));
  student_drop_main main_8 (
    .\input (rom_7_data), .send(send_6), .\output (main_8_output), .catch(main_14_catch), .clk(clock_3_out));
  student_catcher_main main_9 (.student(main_3_output), .catch(main_9_catch), .profesor(rom_1_data));
  student_catcher_main main_10 (.student(main_4_output), .catch(main_10_catch), .profesor(rom_1_data));
  student_catcher_main main_11 (.student(main_5_output), .catch(main_11_catch), .profesor(rom_1_data));
  student_catcher_main main_12 (.student(main_6_output), .catch(main_12_catch), .profesor(rom_1_data));
  student_catcher_main main_13 (.student(main_7_output), .catch(main_13_catch), .profesor(rom_1_data));
  student_catcher_main main_14 (.student(main_8_output), .catch(main_14_catch), .profesor(rom_1_data));
  assign or_2_out = main_3_output | main_4_output | main_5_output | rom_1_data | main_6_output | main_7_output | main_8_output;  // OR_Gate or_2, 32 bits wide
  or or_3 (or_3_out, main_14_catch, main_13_catch, main_12_catch, main_11_catch, main_10_catch, main_9_catch);
  and and_1 (and_1_out, or_3_out, clock_1_out);
  DotMatrix #(.matrixcols(32), .matrixrows(32)) dotmatrix_1 (
    .col0(main_15_out_4), .col1(main_15_out_5), .col2(main_15_out_6), .col3(main_15_out_7),
    .col4(main_15_out_8), .col5(main_15_out_9), .col6(main_15_out_10), .col7(main_15_out_11),
    .col8(main_15_out_12), .col9(main_15_out_13), .col10(main_15_out_14), .col11(main_15_out_15),
    .col12(main_15_out_16), .col13(main_15_out_17), .col14(main_15_out_18), .col15(main_15_out_19),
    .col16(main_15_out_20), .col17(main_15_out_21), .col18(main_15_out_22), .col19(main_15_out_23),
    .col20(main_15_out_24), .col21(main_15_out_25), .col22(main_15_out_26), .col23(main_15_out_27),
    .col24(main_15_out_28), .col25(main_15_out_29), .col26(main_15_out_30), .col27(main_15_out_31),
    .col28(main_15_out_32), .col29(main_15_out_33), .col30(main_15_out_34), .col31(main_15_out_35));
  display_buffer_main main_15 (
    .Address(or_2_out), .Select(counter_2_q), .out_4(main_15_out_4), .out_5(main_15_out_5),
    .out_6(main_15_out_6), .out_7(main_15_out_7), .out_8(main_15_out_8), .out_9(main_15_out_9),
    .out_10(main_15_out_10), .out_11(main_15_out_11), .out_12(main_15_out_12), .out_13(main_15_out_13),
    .out_14(main_15_out_14), .out_15(main_15_out_15), .out_16(main_15_out_16), .out_17(main_15_out_17),
    .out_18(main_15_out_18), .out_19(main_15_out_19), .out_20(main_15_out_20), .out_21(main_15_out_21),
    .out_22(main_15_out_22), .out_23(main_15_out_23), .out_24(main_15_out_24), .out_25(main_15_out_25),
    .out_26(main_15_out_26), .out_27(main_15_out_27), .out_28(main_15_out_28), .out_29(main_15_out_29),
    .out_30(main_15_out_30), .out_31(main_15_out_31), .out_32(main_15_out_32), .out_33(main_15_out_33),
    .out_34(main_15_out_34), .out_35(main_15_out_35), .Done(main_15_done));
  Counter #(.width(10), .max('h3ff), .ongoal("stay")) counter_3 (
    .Q(counter_3_q), .clk(or_3_out));  // open: load, D, count, carry, clr
  Counter #(.width(10), .max('h3ff), .ongoal("stay")) counter_4 (
    .Q(counter_4_q), .clk(and_1_out));  // open: load, D, count, carry, clr
  Divider #(.width(10)) divider_1 (.a(counter_3_q), .b(10'h2));  // open: out, upper, rem
  Multiplier #(.width(10)) multiplier_1 (.a(counter_4_q), .b(10'h2), .out(multiplier_1_out));  // open: cin, cout
  ROM #(.addrWidth(10), .dataWidth(24)) rom_8 (.addr(multiplier_1_out), .data(rom_8_data));  // open: sel
  _7_Segment_Display u_7_segment_display_1 (
    .g(rom_8_data[17]), .f(rom_8_data[18]), .a(rom_8_data[23]), .b(rom_8_data[22]), .e(rom_8_data[19]),
    .d(rom_8_data[20]), .c(rom_8_data[21]), .dp(rom_8_data[16]));
  _7_Segment_Display u_7_segment_display_2 (
    .g(rom_8_data[9]), .f(rom_8_data[10]), .a(rom_8_data[15]), .b(rom_8_data[14]), .e(rom_8_data[11]),
    .d(rom_8_data[12]), .c(rom_8_data[13]), .dp(rom_8_data[8]));
  _7_Segment_Display u_7_segment_display_3 (
    .g(rom_8_data[1]), .f(rom_8_data[2]), .a(rom_8_data[7]), .b(rom_8_data[6]), .e(rom_8_data[3]),
    .d(rom_8_data[4]), .c(rom_8_data[5]), .dp(rom_8_data[0]));

  // Notes on the sheet:
  //   keyboard
  //   a
  //   d
  //   Zegar:szybko
  //   A6
  //   A5
  //   A4
  //   A3
  //   A2
  //   A1
  //   contents of rom_1 (hex, n*v repeats v):
  //   27*0 4 7 e 7 4
  //   profesor
  //   contents of rom_2 (hex, n*v repeats v):
  //   0 50000000 e0000000 50000000
  //   contents of rom_3 (hex, n*v repeats v):
  //   6*0 50000000 e0000000 50000000
  //   contents of rom_4 (hex, n*v repeats v):
  //   12*0 50000000 e0000000 50000000
  //   contents of rom_5 (hex, n*v repeats v):
  //   17*0 50000000 e0000000 50000000
  //   contents of rom_6 (hex, n*v repeats v):
  //   23*0 50000000 e0000000 50000000
  //   contents of rom_7 (hex, n*v repeats v):
  //   28*0 50000000 e0000000 50000000
  //   Liczba zlapanych studentow:
  //   contents of rom_8 (hex, n*v repeats v):
  //   fcfcfc fcfc60 fcfcda fcfcf2 fcfc66 fcfcb6 fcfcbf fcfce0 fcfcfe fcfcf7 fc60fc fc6060 fc60da fc60f2
  //   fc6066 fc60b6 fc60bf fc60e0 fc60fe fc60f7 fcdafc fcda60 fcdada fcdaf2 fcda66 fcdab6 fcdabf fcdae0
  //   fcdafe fcdaf7 fcf2fc fcf260 fcf2da fcf2f2 fcf266 fcf2b6 fcf2bf fcf2e0 fcf2fe fcf2f7 fc66fc fc6660
  //   fc66da fc66f2 fc6666 fc66b6 fc66bf fc66e0 fc66fe fc66f7 fcb6fc fcb660 fcb6da fcb6f2 fcb666 fcb6b6
  //   fcb6bf fcb6e0 fcb6fe fcb6f7 fcbffc fcbf60 fcbfda fcbff2 fcbf66 fcbfb6 fcbfbf fcbfe0 fcbffe fcbff7
  //   fce0fc fce060 fce0da fce0f2 fce066 fce0b6 fce0bf fce0e0 fce0fe fce0f7 fcfefc fcfe60 fcfeda fcfef2
  //   fcfe66 fcfeb6 fcfebf fcfee0 fcfefe fcfef7 fcf7fc fcf760 fcf7da fcf7f2 fcf766 fcf7b6 fcf7bf fcf7e0
  //   fcf7fe fcf7f7 60fcfc 60fc60 60fcda 60fcf2 60fc66 60fcb6 60fcbf 60fce0 60fcfe 60fcf7 6060fc 606060
  //   6060da 6060f2 606066 6060b6 6060bf 6060e0 6060fe 6060f7 60dafc 60da60 60dada 60daf2 60da66 60dab6
  //   60dabf 60dae0 60dafe 60daf7 60f2fc 60f260 60f2da 60f2f2 60f266 60f2b6 60f2bf 60f2e0 60f2fe 60f2f7
  //   6066fc 606660 6066da 6066f2 606666 6066b6 6066bf 6066e0 6066fe 6066f7 60b6fc 60b660 60b6da 60b6f2
  //   60b666 60b6b6 60b6bf 60b6e0 60b6fe 60b6f7 60bffc 60bf60 60bfda 60bff2 60bf66 60bfb6 60bfbf 60bfe0
  //   60bffe 60bff7 60e0fc 60e060 60e0da 60e0f2 60e066 60e0b6 60e0bf 60e0e0 60e0fe 60e0f7 60fefc 60fe60
  //   60feda 60fef2 60fe66 60feb6 60febf 60fee0 60fefe 60fef7 60f7fc 60f760 60f7da 60f7f2 60f766 60f7b6
  //   60f7bf 60f7e0 60f7fe 60f7f7 dafcfc dafc60 dafcda dafcf2 dafc66 dafcb6 dafcbf dafce0 dafcfe dafcf7
  //   da60fc da6060 da60da da60f2 da6066 da60b6 da60bf da60e0 da60fe da60f7 dadafc dada60 dadada dadaf2
  //   dada66 dadab6 dadabf dadae0 dadafe dadaf7 daf2fc daf260 daf2da daf2f2 daf266 daf2b6 daf2bf daf2e0
  //   daf2fe daf2f7 da66fc da6660 da66da da66f2 da6666 da66b6 da66bf da66e0 da66fe da66f7 dab6fc dab660
  //   dab6da dab6f2 dab666 dab6b6 dab6bf dab6e0 dab6fe dab6f7 dabffc dabf60 dabfda dabff2 dabf66 dabfb6
  //   dabfbf dabfe0 dabffe dabff7 dae0fc dae060 dae0da dae0f2 dae066 dae0b6 dae0bf dae0e0 dae0fe dae0f7
  //   dafefc dafe60 dafeda dafef2 dafe66 dafeb6 dafebf dafee0 dafefe dafef7 daf7fc daf760 daf7da daf7f2
  //   daf766 daf7b6 daf7bf daf7e0 daf7fe daf7f7 f2fcfc f2fc60 f2fcda f2fcf2 f2fc66 f2fcb6 f2fcbf f2fce0
  //   f2fcfe f2fcf7 f260fc f26060 f260da f260f2 f26066 f260b6 f260bf f260e0 f260fe f260f7 f2dafc f2da60
  //   f2dada f2daf2 f2da66 f2dab6 f2dabf f2dae0 f2dafe f2daf7 f2f2fc f2f260 f2f2da f2f2f2 f2f266 f2f2b6
  //   f2f2bf f2f2e0 f2f2fe f2f2f7 f266fc f26660 f266da f266f2 f26666 f266b6 f266bf f266e0 f266fe f266f7
  //   f2b6fc f2b660 f2b6da f2b6f2 f2b666 f2b6b6 f2b6bf f2b6e0 f2b6fe f2b6f7 f2bffc f2bf60 f2bfda f2bff2
  //   f2bf66 f2bfb6 f2bfbf f2bfe0 f2bffe f2bff7 f2e0fc f2e060 f2e0da f2e0f2 f2e066 f2e0b6 f2e0bf f2e0e0
  //   f2e0fe f2e0f7 f2fefc f2fe60 f2feda f2fef2 f2fe66 f2feb6 f2febf f2fee0 f2fefe f2fef7 f2f7fc f2f760
  //   f2f7da f2f7f2 f2f766 f2f7b6 f2f7bf f2f7e0 f2f7fe f2f7f7 66fcfc 66fc60 66fcda 66fcf2 66fc66 66fcb6
  //   66fcbf 66fce0 66fcfe 66fcf7 6660fc 666060 6660da 6660f2 666066 6660b6 6660bf 6660e0 6660fe 6660f7
  //   66dafc 66da60 66dada 66daf2 66da66 66dab6 66dabf 66dae0 66dafe 66daf7 66f2fc 66f260 66f2da 66f2f2
  //   66f266 66f2b6 66f2bf 66f2e0 66f2fe 66f2f7 6666fc 666660 6666da 6666f2 666666 6666b6 6666bf 6666e0
  //   6666fe 6666f7 66b6fc 66b660 66b6da 66b6f2 66b666 66b6b6 66b6bf 66b6e0 66b6fe 66b6f7 66bffc 66bf60
  //   66bfda 66bff2 66bf66 66bfb6 66bfbf 66bfe0 66bffe 66bff7 66e0fc 66e060 66e0da 66e0f2 66e066 66e0b6
  //   66e0bf 66e0e0 66e0fe 66e0f7 66fefc 66fe60 66feda 66fef2 66fe66 66feb6 66febf 66fee0 66fefe 66fef7
  //   66f7fc 66f760 66f7da 66f7f2 66f766 66f7b6 66f7bf 66f7e0 66f7fe 66f7f7 b6fcfc b6fc60 b6fcda b6fcf2
  //   b6fc66 b6fcb6 b6fcbf b6fce0 b6fcfe b6fcf7 b660fc b66060 b660da b660f2 b66066 b660b6 b660bf b660e0
  //   b660fe b660f7 b6dafc b6da60 b6dada b6daf2 b6da66 b6dab6 b6dabf b6dae0 b6dafe b6daf7 b6f2fc b6f260
  //   b6f2da b6f2f2 b6f266 b6f2b6 b6f2bf b6f2e0 b6f2fe b6f2f7 b666fc b66660 b666da b666f2 b66666 b666b6
  //   b666bf b666e0 b666fe b666f7 b6b6fc b6b660 b6b6da b6b6f2 b6b666 b6b6b6 b6b6bf b6b6e0 b6b6fe b6b6f7
  //   b6bffc b6bf60 b6bfda b6bff2 b6bf66 b6bfb6 b6bfbf b6bfe0 b6bffe b6bff7 b6e0fc b6e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
endmodule
